// Logisim project ALUpj3.circ as structural Verilog
module ALU (
  input  [31:0] High_Numero_Uno,
  input  [31:0] High_Numero_dos,
  input  [4:0] Corrimientos,
  input  [31:0] Low_Numero_uno,
  input  [31:0] Low_Numero_Dos,
  input  [3:0] in_6,
  output [31:0] out_7,
  output [31:0] out_8
);

  wire adder_2_cout, subtractor_2_bout;
  wire [31:0] adder_1_out, adder_2_out, and_1_out, and_2_out, or_1_out, or_2_out, shift_left_1_salida_high,
       shift_left_1_salida_low, shift_right_1_salida_high, shift_right_1_salida_low, shifter_1_out,
       shifter_2_out, shifter_3_out, shifter_4_out, subtractor_1_out, subtractor_2_out, xor_1_out, xor_2_out;

  Adder #(.width(32)) adder_1 (
    .a(High_Numero_Uno), .b(High_Numero_dos), .out(adder_1_out), .cin(adder_2_cout));  // open: cout
  Subtractor #(.width(32)) subtractor_1 (
    .a(High_Numero_Uno), .b(High_Numero_dos), .out(subtractor_1_out), .bin(subtractor_2_bout));  // open: bout
  assign and_1_out = High_Numero_Uno & High_Numero_dos;  // AND_Gate and_1, 32 bits wide
  assign or_1_out = High_Numero_Uno | High_Numero_dos;  // OR_Gate or_1, 32 bits wide
  assign xor_1_out = High_Numero_Uno ^ High_Numero_dos;  // XOR_Gate xor_1, 32 bits wide
  Shift_Left shift_left_1 (
    .High(High_Numero_dos), .Corrimiento(Corrimientos), .Low(Low_Numero_Dos),
    .Salida_high(shift_left_1_salida_high), .Salida_low(shift_left_1_salida_low));
  Shift_right shift_right_1 (
    .High(High_Numero_Uno), .Corrimiento(Corrimientos), .Low(Low_Numero_uno),
    .Salida_high(shift_right_1_salida_high), .Salida_Low(shift_right_1_salida_low));
  Shifter #(.width(32), .shift("ar")) shifter_1 (.out(shifter_1_out));  // open: in, dist
  Shifter #(.width(32), .shift("rr")) shifter_2 (.out(shifter_2_out));  // open: in, dist
  Adder #(.width(32)) adder_2 (
    .a(Low_Numero_uno), .b(Low_Numero_Dos), .out(adder_2_out), .cout(adder_2_cout));  // open: cin
  Subtractor #(.width(32)) subtractor_2 (
    .a(Low_Numero_uno), .b(Low_Numero_Dos), .out(subtractor_2_out), .bout(subtractor_2_bout));  // open: bin
  assign and_2_out = Low_Numero_uno & Low_Numero_Dos;  // AND_Gate and_2, 32 bits wide
  assign or_2_out = Low_Numero_uno | Low_Numero_Dos;  // OR_Gate or_2, 32 bits wide
  assign xor_2_out = Low_Numero_uno ^ Low_Numero_Dos;  // XOR_Gate xor_2, 32 bits wide
  Shifter #(.width(32), .shift("ar")) shifter_3 (.out(shifter_3_out));  // open: in, dist
  Shifter #(.width(32), .shift("rr")) shifter_4 (.out(shifter_4_out));  // open: in, dist
  Multiplexer #(.select(4), .width(32)) multiplexer_1 (
    .in0(adder_1_out), .in1(subtractor_1_out), .in2(and_1_out), .in3(or_1_out), .in4(xor_1_out),
    .in5(shift_left_1_salida_high), .in6(shift_right_1_salida_high), .in7(shifter_1_out),
    .in8(shifter_2_out), .in9({32{1'b0}}), .in10({32{1'b0}}), .in11({32{1'b0}}), .in12({32{1'b0}}),
    .in13({32{1'b0}}), .in14({32{1'b0}}), .in15({32{1'b0}}), .out(out_7), .sel(in_6), .en(1'b1));
  Multiplexer #(.select(4), .width(32)) multiplexer_2 (
    .in0(adder_2_out), .in1(subtractor_2_out), .in2(and_2_out), .in3(or_2_out), .in4(xor_2_out),
    .in5(shift_left_1_salida_low), .in6(shift_right_1_salida_low), .in7(shifter_3_out), .in8(shifter_4_out),
    .in9({32{1'b0}}), .in10({32{1'b0}}), .in11({32{1'b0}}), .in12({32{1'b0}}), .in13({32{1'b0}}),
    .in14({32{1'b0}}), .in15({32{1'b0}}), .out(out_8), .sel(in_6), .en(1'b1));
endmodule

module Register_File (
  input  in_1,
  input  in_2,
  input  in_3,
  input  in_4,
  input  in_5,
  input  in_6,
  input  [31:0] in_7,
  output [4:0] out_8,
  output [31:0] out_9
);

  wire and_1_out, and_2_out, and_3_out, and_4_out, and_5_out, and_6_out, and_7_out, and_8_out, and_9_out,
       and_10_out, and_11_out, and_12_out, and_13_out, and_14_out, and_15_out, and_16_out, and_17_out,
       and_18_out, and_19_out, and_20_out, and_21_out, and_22_out, and_23_out, and_24_out, and_25_out,
       and_26_out, and_27_out, and_28_out, and_29_out, and_30_out, and_31_out, and_32_out, not_1_out,
       not_2_out, not_3_out, not_4_out, not_5_out, not_6_out, not_7_out, not_8_out, not_9_out, not_10_out,
       not_11_out, not_12_out, not_13_out, not_14_out, not_15_out, not_16_out, not_17_out, not_18_out,
       not_19_out, not_20_out, not_21_out, not_22_out, not_23_out, not_24_out, not_25_out, not_26_out,
       not_27_out, not_28_out, not_29_out, not_30_out, not_31_out, not_32_out, not_33_out, not_34_out,
       not_35_out, not_36_out, not_37_out, not_38_out, not_39_out, not_40_out, not_41_out, not_42_out,
       not_43_out, not_44_out, not_45_out, not_46_out, not_47_out, not_48_out, not_49_out, not_50_out,
       not_51_out, not_52_out, not_53_out, not_54_out, not_55_out, not_56_out, not_57_out, not_58_out,
       not_59_out, not_60_out, not_61_out, not_62_out, not_63_out, not_64_out, not_65_out, not_66_out,
       not_67_out, not_68_out, not_69_out, not_70_out, not_71_out, not_72_out, not_73_out, not_74_out,
       not_75_out, not_76_out, not_77_out, not_78_out, not_79_out, not_80_out;
  wire [31:0] undriven, undriven_2, undriven_3, undriven_4, undriven_5, x0_q, x1_q, x3_q, x4_2_q, x4_3_q,
       x4_q, x6_q, x7_q, x8_q, x9_2_q, x9_q, x11_q, x12_q, x13_q, x14_q, x15_q, x16_q, x17_q, x18_q, x19_q,
       x20_q, x21_2_q, x21_q, x23_2_q, x23_q, x25_q, x26_q, x27_q, x28_q, x29_q, x30_q, x31_q;

  not not_1 (not_1_out, in_4);
  not not_2 (not_2_out, in_3);
  not not_3 (not_3_out, in_2);
  not not_4 (not_4_out, in_1);
  not not_5 (not_5_out, in_5);
  not not_6 (not_6_out, in_3);
  not not_7 (not_7_out, in_2);
  not not_8 (not_8_out, in_1);
  not not_9 (not_9_out, in_3);
  not not_10 (not_10_out, in_2);
  not not_11 (not_11_out, in_1);
  not not_12 (not_12_out, in_5);
  not not_13 (not_13_out, in_4);
  not not_14 (not_14_out, in_2);
  not not_15 (not_15_out, in_1);
  not not_16 (not_16_out, in_4);
  not not_17 (not_17_out, in_2);
  not not_18 (not_18_out, in_1);
  not not_19 (not_19_out, in_5);
  not not_20 (not_20_out, in_2);
  not not_21 (not_21_out, in_1);
  not not_22 (not_22_out, in_2);
  not not_23 (not_23_out, in_1);
  not not_24 (not_24_out, in_5);
  not not_25 (not_25_out, in_4);
  not not_26 (not_26_out, in_3);
  not not_27 (not_27_out, in_1);
  not not_28 (not_28_out, in_4);
  not not_29 (not_29_out, in_3);
  not not_30 (not_30_out, in_1);
  not not_31 (not_31_out, in_5);
  not not_32 (not_32_out, in_3);
  not not_33 (not_33_out, in_1);
  not not_34 (not_34_out, in_3);
  not not_35 (not_35_out, in_1);
  not not_36 (not_36_out, in_5);
  not not_37 (not_37_out, in_4);
  not not_38 (not_38_out, in_1);
  not not_39 (not_39_out, in_4);
  not not_40 (not_40_out, in_1);
  not not_41 (not_41_out, in_5);
  not not_42 (not_42_out, in_1);
  not not_43 (not_43_out, in_1);
  not not_44 (not_44_out, in_5);
  not not_45 (not_45_out, in_4);
  not not_46 (not_46_out, in_3);
  not not_47 (not_47_out, in_2);
  not not_48 (not_48_out, in_4);
  not not_49 (not_49_out, in_3);
  not not_50 (not_50_out, in_2);
  not not_51 (not_51_out, in_5);
  not not_52 (not_52_out, in_3);
  not not_53 (not_53_out, in_2);
  not not_54 (not_54_out, in_3);
  not not_55 (not_55_out, in_2);
  not not_56 (not_56_out, in_5);
  not not_57 (not_57_out, in_4);
  not not_58 (not_58_out, in_2);
  not not_59 (not_59_out, in_4);
  not not_60 (not_60_out, in_2);
  not not_61 (not_61_out, in_5);
  not not_62 (not_62_out, in_2);
  not not_63 (not_63_out, in_2);
  not not_64 (not_64_out, in_5);
  not not_65 (not_65_out, in_4);
  not not_66 (not_66_out, in_3);
  not not_67 (not_67_out, in_4);
  not not_68 (not_68_out, in_3);
  not not_69 (not_69_out, in_5);
  not not_70 (not_70_out, in_3);
  not not_71 (not_71_out, in_3);
  not not_72 (not_72_out, in_5);
  not not_73 (not_73_out, in_4);
  not not_74 (not_74_out, in_4);
  not not_75 (not_75_out, in_5);
  not not_76 (not_76_out, in_5);
  not not_77 (not_77_out, in_4);
  not not_78 (not_78_out, in_3);
  not not_79 (not_79_out, in_2);
  not not_80 (not_80_out, in_1);
  and and_1 (and_1_out, in_5, not_1_out, not_2_out, not_3_out, not_4_out);
  and and_2 (and_2_out, not_5_out, in_4, not_6_out, not_7_out, not_8_out);
  and and_3 (and_3_out, in_5, in_4, not_9_out, not_10_out, not_11_out);
  and and_4 (and_4_out, not_12_out, not_13_out, in_3, not_14_out, not_15_out);
  and and_5 (and_5_out, in_5, not_16_out, in_3, not_17_out, not_18_out);
  and and_6 (and_6_out, not_19_out, in_4, in_3, not_20_out, not_21_out);
  and and_7 (and_7_out, in_5, in_4, in_3, not_22_out, not_23_out);
  and and_8 (and_8_out, not_24_out, not_25_out, not_26_out, in_2, not_27_out);
  and and_9 (and_9_out, in_5, not_28_out, not_29_out, in_2, not_30_out);
  and and_10 (and_10_out, not_31_out, in_4, not_32_out, in_2, not_33_out);
  and and_11 (and_11_out, in_5, in_4, not_34_out, in_2, not_35_out);
  and and_12 (and_12_out, not_36_out, not_37_out, in_3, in_2, not_38_out);
  and and_13 (and_13_out, in_5, not_39_out, in_3, in_2, not_40_out);
  and and_14 (and_14_out, not_41_out, in_4, in_3, in_2, not_42_out);
  and and_15 (and_15_out, in_5, in_4, in_3, in_2, not_43_out);
  and and_16 (and_16_out, not_44_out, not_45_out, not_46_out, not_47_out, in_1);
  and and_17 (and_17_out, in_5, not_48_out, not_49_out, not_50_out, in_1);
  and and_18 (and_18_out, not_51_out, in_4, not_52_out, not_53_out, in_1);
  and and_19 (and_19_out, in_5, in_4, not_54_out, not_55_out, in_1);
  and and_20 (and_20_out, not_56_out, not_57_out, in_3, not_58_out, in_1);
  and and_21 (and_21_out, in_5, not_59_out, in_3, not_60_out, in_1);
  and and_22 (and_22_out, not_61_out, in_4, in_3, not_62_out, in_1);
  and and_23 (and_23_out, in_5, in_4, in_3, not_63_out, in_1);
  and and_24 (and_24_out, not_64_out, not_65_out, not_66_out, in_2, in_1);
  and and_25 (and_25_out, in_5, not_67_out, not_68_out, in_2, in_1);
  and and_26 (and_26_out, not_69_out, in_4, not_70_out, in_2, in_1);
  and and_27 (and_27_out, in_5, in_4, not_71_out, in_2, in_1);
  and and_28 (and_28_out, not_72_out, not_73_out, in_3, in_2, in_1);
  and and_29 (and_29_out, in_5, not_74_out, in_3, in_2, in_1);
  and and_30 (and_30_out, not_75_out, in_4, in_3, in_2, in_1);
  and and_31 (and_31_out, in_5, in_4, in_3, in_2, in_1);
  and and_32 (and_32_out, not_76_out, not_77_out, not_78_out, not_79_out, not_80_out);
  Register #(.width(32)) x1 (.D(in_7), .en(and_1_out), .Q(x1_q), .clk(in_6));  // open: clr
  Register #(.width(32)) x4 (.D(in_7), .en(and_2_out), .Q(x4_q), .clk(in_6));  // open: clr
  Register #(.width(32)) x3 (.D(in_7), .en(and_3_out), .Q(x3_q), .clk(in_6));  // open: clr
  Register #(.width(32)) x4_2 (.D(in_7), .en(and_4_out), .Q(x4_2_q), .clk(in_6));  // open: clr
  Register #(.width(32)) x4_3 (.D(in_7), .en(and_5_out), .Q(x4_3_q), .clk(in_6));  // open: clr
  Register #(.width(32)) x6 (.D(in_7), .en(and_6_out), .Q(x6_q), .clk(in_6));  // open: clr
  Register #(.width(32)) x7 (.D(in_7), .en(and_7_out), .Q(x7_q), .clk(in_6));  // open: clr
  Register #(.width(32)) x8 (.D(in_7), .en(and_8_out), .Q(x8_q), .clk(in_6));  // open: clr
  Register #(.width(32)) x9 (.D(in_7), .en(and_9_out), .Q(x9_q), .clk(in_6));  // open: clr
  Register #(.width(32)) x9_2 (.D(in_7), .en(and_10_out), .Q(x9_2_q), .clk(in_6));  // open: clr
  Register #(.width(32)) x11 (.D(in_7), .en(and_11_out), .Q(x11_q), .clk(in_6));  // open: clr
  Register #(.width(32)) x12 (.D(in_7), .en(and_12_out), .Q(x12_q), .clk(in_6));  // open: clr
  Register #(.width(32)) x13 (.D(in_7), .en(and_13_out), .Q(x13_q), .clk(in_6));  // open: clr
  Register #(.width(32)) x14 (.D(in_7), .en(and_14_out), .Q(x14_q), .clk(in_6));  // open: clr
  Register #(.width(32)) x15 (.D(in_7), .en(and_15_out), .Q(x15_q), .clk(in_6));  // open: clr
  Register #(.width(32)) x16 (.D(undriven), .en(and_16_out), .Q(x16_q), .clk(in_6));  // open: clr
  Register #(.width(32)) x17 (.D(undriven_2), .en(and_17_out), .Q(x17_q), .clk(in_6));  // open: clr
  Register #(.width(32)) x18 (.D(in_7), .en(and_18_out), .Q(x18_q), .clk(in_6));  // open: clr
  Register #(.width(32)) x19 (.D(in_7), .en(and_19_out), .Q(x19_q), .clk(in_6));  // open: clr
  Register #(.width(32)) x20 (.D(in_7), .en(and_20_out), .Q(x20_q), .clk(in_6));  // open: clr
  Register #(.width(32)) x21 (.D(in_7), .en(and_21_out), .Q(x21_q), .clk(in_6));  // open: clr
  Register #(.width(32)) x21_2 (.D(in_7), .en(and_22_out), .Q(x21_2_q), .clk(in_6));  // open: clr
  Register #(.width(32)) x23 (.D(in_7), .en(and_23_out), .Q(x23_q), .clk(in_6));  // open: clr
  Register #(.width(32)) x23_2 (.D(in_7), .en(and_24_out), .Q(x23_2_q), .clk(in_6));  // open: clr
  Register #(.width(32)) x25 (.D(in_7), .en(and_25_out), .Q(x25_q), .clk(in_6));  // open: clr
  Register #(.width(32)) x26 (.D(in_7), .en(and_26_out), .Q(x26_q), .clk(in_6));  // open: clr
  Register #(.width(32)) x27 (.D(in_7), .en(and_27_out), .Q(x27_q), .clk(in_6));  // open: clr
  Register #(.width(32)) x28 (.D(in_7), .en(and_28_out), .Q(x28_q), .clk(in_6));  // open: clr
  Register #(.width(32)) x29 (.D(in_7), .en(and_29_out), .Q(x29_q), .clk(in_6));  // open: clr
  Register #(.width(32)) x30 (.D(in_7), .en(and_30_out), .Q(x30_q), .clk(in_6));  // open: clr
  Register #(.width(32)) x31 (.D(in_7), .en(and_31_out), .Q(x31_q), .clk(in_6));  // open: clr
  Register #(.width(32)) x0 (.D(in_7), .en(and_32_out), .Q(x0_q), .clk(in_6));  // open: clr
  Multiplexer #(.select(5), .width(32)) multiplexer_1 (
    .in0(x0_q), .in1(x1_q), .in2(undriven_4), .in3(undriven_5), .in4(x4_2_q), .in5(x4_3_q), .in6(x6_q),
    .in7(undriven_3), .in8(x8_q), .in9(x9_q), .in10(x9_2_q), .in11(x11_q), .in12(x12_q), .in13(x13_q),
    .in14(x14_q), .in15(x15_q), .in16(x16_q), .in17(x17_q), .in18(x18_q), .in19(x19_q), .in20(x20_q),
    .in21(x21_q), .in22(x21_2_q), .in23(x23_q), .in24(x23_2_q), .in25(x25_q), .in26(x26_q), .in27(x27_q),
    .in28(x28_q), .in29(x29_q), .in30(x30_q), .in31(x31_q), .out(out_9), .sel({in_1, in_2, in_3, in_4, in_5}));  // open: en

  assign out_8 = {in_1, in_2, in_3, in_4, in_5};
endmodule

module Shift_Left (
  input  [31:0] High,
  input  [4:0] Corrimiento,
  input  [31:0] Low,
  output [31:0] Salida_high,
  output [31:0] Salida_low
);

  wire [4:0] subtractor_1_out;
  wire [31:0] or_1_out, shifter_1_out, shifter_2_out;

  Subtractor #(.width(5)) subtractor_1 (.a({5{1'b1}}), .b(Corrimiento), .out(subtractor_1_out));  // open: bin, bout
  Shifter #(.width(32)) shifter_1 (.in(High), .\dist (Corrimiento), .out(shifter_1_out));
  assign or_1_out = Low | {32{1'b0}};  // OR_Gate or_1, 32 bits wide
  Shifter #(.width(32), .shift("lr")) shifter_2 (.in(or_1_out), .\dist (subtractor_1_out), .out(shifter_2_out));
  assign Salida_high = shifter_1_out | shifter_2_out;  // OR_Gate or_2, 32 bits wide
  Shifter #(.width(32)) shifter_3 (.in(Low), .\dist (Corrimiento), .out(Salida_low));
endmodule

module Shift_right (
  input  [31:0] High,
  input  [4:0] Corrimiento,
  input  [31:0] Low,
  output [31:0] Salida_high,
  output [31:0] Salida_Low
);

  wire [4:0] subtractor_1_out;
  wire [31:0] or_1_out, shifter_1_out, shifter_3_out;

  Subtractor #(.width(5)) subtractor_1 (.a({5{1'b1}}), .b(Corrimiento), .out(subtractor_1_out));  // open: bin, bout
  assign or_1_out = High | {32{1'b0}};  // OR_Gate or_1, 32 bits wide
  Shifter #(.width(32), .shift("lr")) shifter_1 (.in(Low), .\dist (Corrimiento), .out(shifter_1_out));
  Shifter #(.width(32), .shift("lr")) shifter_2 (.in(High), .\dist (Corrimiento), .out(Salida_high));
  Shifter #(.width(32)) shifter_3 (.in(or_1_out), .\dist (subtractor_1_out), .out(shifter_3_out));
  assign Salida_Low = shifter_3_out | shifter_1_out;  // OR_Gate or_2, 32 bits wide
endmodule

module Prueba_registro (
  input  [3:0] in_1,
  input  in_2,
  output [3:0] out_3
);

  Register #(.width(4)) register_1 (.D(in_1), .Q(out_3), .clk(in_2));  // open: en, clr
endmodule
